// Logisim project singlecycle_diagram.circ as structural Verilog: 14 circuits, main circuit core
module core (
);

  wire cpumembundle_1_out_9, cpumembundle_1_out_10, cpumembundle_1_out_11, cpumembundle_1_out_12,
       cpumembundle_1_out_13, cpumembundle_1_out_14, cpumembundle_1_out_15, cpumembundle_1_out_16,
       decisionsalto_1_jump_flag, id_1_alu_op1_src, id_1_alu_op2_src, id_1_mem_read_en, id_1_mem_wr_en,
       id_1_reg_wr_en, id_1_wb_src, undriven, undriven_4;
  wire [2:0] memory_1_instruction_3;
  wire [3:0] alucontrol_1_alu_func;
  wire [4:0] id_1_reg_wr_addr, id_1_rs1_addr, id_1_rs2_addr;
  wire [6:0] memory_1_instruction, memory_1_instruction_4;
  wire [7:0] undriven_3;
  wire [24:7] memory_1_instruction_2;
  wire [31:0] alu_1_res, id_1_ex_imm, memaccess_1_wb_mem_read_data, mux2_1_out_4, mux2_2_out_4,
       mux2invertido_1_val_out, mux2invertido_2_val_out, mux3_1_val_out, pc_1_instr_addr_post,
       rf_1_read_data1, rf_1_read_data2, sum_1_res, sum_2_res, undriven_2;

  mux2invertido mux2invertido_1 (
    .in1(sum_2_res), .in2(sum_1_res), .sel(decisionsalto_1_jump_flag), .val_out(mux2invertido_1_val_out));
  PC pc_1 (.clk(undriven), .instr_addr_pre(mux2invertido_1_val_out), .instr_addr_post(pc_1_instr_addr_post));
  sum sum_1 (.op1(pc_1_instr_addr_post), .op2(undriven_2), .res(sum_1_res));
  memory memory_1 (
    .instruction_address(pc_1_instr_addr_post), .in_2(undriven_3[7]), .in_3(undriven_3[6]),
    .in_4(undriven_3[5]), .in_5(undriven_3[0]), .in_6(undriven_3[1]), .in_7(undriven_3[2]),
    .in_8(undriven_3[4]), .in_9(undriven_3[3]),
    .instruction({memory_1_instruction_4, memory_1_instruction_2[24:15], memory_1_instruction_3, memory_1_instruction_2[11:7], memory_1_instruction}));
  ID id_1 (
    .instruction({memory_1_instruction_4, memory_1_instruction_2[24:15], memory_1_instruction_3, memory_1_instruction_2[11:7], memory_1_instruction}),
    .rs2_addr(id_1_rs2_addr), .ex_imm(id_1_ex_imm), .alu_op1_src(id_1_alu_op1_src),
    .alu_op2_src(id_1_alu_op2_src), .mem_read_en(id_1_mem_read_en), .mem_wr_en(id_1_mem_wr_en),
    .wb_src(id_1_wb_src), .reg_wr_en(id_1_reg_wr_en), .reg_wr_addr(id_1_reg_wr_addr), .rs1_addr(id_1_rs1_addr));
  RF rf_1 (
    .wr_addr(id_1_reg_wr_addr), .wr_data(mux3_1_val_out), .rs1_addr(id_1_rs1_addr), .rs2_addr(id_1_rs2_addr),
    .wr_en(id_1_reg_wr_en), .read_data2(rf_1_read_data2), .read_data1(rf_1_read_data1));
  mux2 mux2_1 (.in_1(id_1_alu_op2_src), .in_2(id_1_ex_imm), .in_3(rf_1_read_data2), .out_4(mux2_1_out_4));
  mux2 mux2_2 (.in_1(id_1_alu_op1_src), .in_2(pc_1_instr_addr_post), .in_3(rf_1_read_data1), .out_4(mux2_2_out_4));
  ALU alu_1 (.op1(mux2_2_out_4), .op2(mux2_1_out_4), .command(alucontrol_1_alu_func), .res(alu_1_res));
  ALUControl alucontrol_1 (
    .func3(memory_1_instruction_3), .func7(memory_1_instruction_4), .opcode(memory_1_instruction),
    .alu_func(alucontrol_1_alu_func));
  DecisionSalto decisionsalto_1 (
    .func3(memory_1_instruction_3), .r1_data(rf_1_read_data2), .r2_data(rf_1_read_data1),
    .opcode(memory_1_instruction), .jump_flag(decisionsalto_1_jump_flag));
  mux2invertido mux2invertido_2 (
    .in1(pc_1_instr_addr_post), .in2(rf_1_read_data1), .sel(undriven_4), .val_out(mux2invertido_2_val_out));
  CPUmemBundle cpumembundle_1 (
    .in_2(undriven_3[6]), .in_3(undriven_3[5]), .in_4(undriven_3[2]), .in_5(undriven_3[1]),
    .in_6(undriven_3[0]), .in_7(undriven_3[4]), .in_8(undriven_3[3]), .in_1(undriven_3[7]),
    .out_10(cpumembundle_1_out_10), .out_11(cpumembundle_1_out_11), .out_12(cpumembundle_1_out_12),
    .out_13(cpumembundle_1_out_13), .out_14(cpumembundle_1_out_14), .out_15(cpumembundle_1_out_15),
    .out_16(cpumembundle_1_out_16), .out_9(cpumembundle_1_out_9));
  sum sum_2 (.op1(id_1_ex_imm), .op2(mux2invertido_2_val_out), .res(sum_2_res));
  MemAccess memaccess_1 (
    .mem_alu_result(alu_1_res), .func3(memory_1_instruction_3), .read_data_2(rf_1_read_data2),
    .mem_read_en(id_1_mem_read_en), .mem_wr_en(id_1_mem_wr_en), .in_6(cpumembundle_1_out_9),
    .in_7(cpumembundle_1_out_10), .in_8(cpumembundle_1_out_11), .in_9(cpumembundle_1_out_12),
    .in_10(cpumembundle_1_out_13), .in_11(cpumembundle_1_out_14), .in_12(cpumembundle_1_out_15),
    .in_13(cpumembundle_1_out_16), .wb_mem_read_data(memaccess_1_wb_mem_read_data));
  mux3 mux3_1 (
    .op2(memaccess_1_wb_mem_read_data), .op3(sum_1_res), .sel(id_1_wb_src), .op1(alu_1_res),
    .val_out(mux3_1_val_out));

  // Notes on the sheet:
  //   jump_address
  //   PC+4
  //   clk
  //   instruction_
  //   address
  //   4
  //   instruction
  //   jump_flag
  //   jump_address
  //   ex_imm
  //   wb_src
  //   instruction_address
  //   rs1_address
  //   rs2_address
  //   reg_wr_address
  //   reg_wr_enable
  //   alu_op1_src
  //   alu_op2_src
  //   mem_read_en
  //   mem_wr_en
  //   func3 (14:12)
  //   func7 (31:25)
  //   opcode (6:0)
  //   opcode
  //   func3
  //   r2_data
  //   r1_data
  //   instruction_address
  //   mem_alu_result
  //   r2_data
  //   func3 (14:12)
  //   r1_data
  //   (opcode = jalr)
  //   wb_mem_read_data
  //   PC+4
endmodule

module PC (
  input  clk,
  input  [31:0] instr_addr_pre,
  output [31:0] instr_addr_post
);
endmodule

module ID (
  input  [31:0] instruction,
  output [4:0] rs1_addr,
  output [4:0] rs2_addr,
  output [31:0] ex_imm,
  output alu_op1_src,
  output alu_op2_src,
  output mem_read_en,
  output mem_wr_en,
  output wb_src,
  output reg_wr_en,
  output [4:0] reg_wr_addr
);
endmodule

module RF (
  input  wr_en,
  input  [4:0] wr_addr,
  input  [31:0] wr_data,
  input  [4:0] rs1_addr,
  input  [4:0] rs2_addr,
  output [31:0] read_data1,
  output [31:0] read_data2
);
endmodule

module memory (
  input  [31:0] instruction_address,
  input  in_2,
  input  in_3,
  input  in_4,
  input  in_5,
  input  in_6,
  input  in_7,
  input  in_8,
  input  in_9,
  output [31:0] instruction
);
endmodule

module mux2 (
  input  in_1,
  input  [31:0] in_2,
  input  [31:0] in_3,
  output [31:0] out_4
);
endmodule

module ALU (
  input  [3:0] command,
  input  [31:0] op1,
  input  [31:0] op2,
  output [31:0] res
);
endmodule

module ALUControl (
  input  [6:0] opcode,
  input  [2:0] func3,
  input  [6:0] func7,
  output [3:0] alu_func
);
endmodule

module DecisionSalto (
  input  [6:0] opcode,
  input  [2:0] func3,
  input  [31:0] r1_data,
  input  [31:0] r2_data,
  output jump_flag
);
endmodule

module mux2invertido (
  input  sel,
  input  [31:0] in1,
  input  [31:0] in2,
  output [31:0] val_out
);
endmodule

module sum (
  input  [31:0] op1,
  input  [31:0] op2,
  output [31:0] res
);
endmodule

module MemAccess (
  input  [31:0] mem_alu_result,
  input  [2:0] func3,
  input  [31:0] read_data_2,
  input  mem_read_en,
  input  mem_wr_en,
  input  in_6,
  input  in_7,
  input  in_8,
  input  in_9,
  input  in_10,
  input  in_11,
  input  in_12,
  input  in_13,
  output [31:0] wb_mem_read_data
);
endmodule

module CPUmemBundle (
  input  in_1,
  input  in_2,
  input  in_3,
  input  in_4,
  input  in_5,
  input  in_6,
  input  in_7,
  input  in_8,
  output out_9,
  output out_10,
  output out_11,
  output out_12,
  output out_13,
  output out_14,
  output out_15,
  output out_16
);
endmodule

module mux3 (
  input  [31:0] op1,
  input  [31:0] op2,
  input  [31:0] op3,
  input  sel,
  output [31:0] val_out
);
endmodule
