// Logisim project mux4cap03.circ as structural Verilog: 2 circuits, main circuit main
module main (
);

  wire [1:0] undriven_5;
  wire [31:0] mux4_1_o, undriven, undriven_2, undriven_3, undriven_4;

  mux4 mux4_1 (.i1(undriven), .i2(undriven_2), .i3(undriven_3), .i4(undriven_4), .sel(undriven_5), .o(mux4_1_o));

  // Notes on the sheet:
  //   sel
  //   i1
  //   i2
  //   o
  //   i3
  //   i4
endmodule

module mux4 (
  input  [31:0] i1,
  input  [31:0] i2,
  input  [31:0] i3,
  input  [31:0] i4,
  input  [1:0] sel,
  output [31:0] o
);
endmodule
